// Logisim project 8bitcomputer.circ as structural Verilog: 2 circuits, main circuit main
module AU (
  input  [7:0] N1,
  input  C_IN,
  input  SUB,
  input  [7:0] N2,
  output [7:0] SUM,
  output C_OUT,
  output ZERO,
  output NEG
);

  wire not_1_out;
  wire [7:0] controlled_buffer_1_out, controlled_buffer_2_out;

  not not_1 (not_1_out, SUB);
  assign controlled_buffer_1_out = SUB ? N2 : 8'bz;  // Controlled_Buffer controlled_buffer_1
  assign controlled_buffer_2_out = not_1_out ? N2 : 8'bz;  // Controlled_Buffer controlled_buffer_2
  Negator negator_1 (.in(controlled_buffer_1_out), .out(controlled_buffer_2_out));
  Adder adder_1 (.a(N1), .b(controlled_buffer_2_out), .out({NEG, SUM[6:0]}), .cin(C_IN), .cout(C_OUT));
  nor nor_1 (ZERO, SUM[0], SUM[1], SUM[2], SUM[3], SUM[4], SUM[5], SUM[6], NEG);

  assign SUM[7] = NEG;
endmodule

module main (
);

  wire and_1_out, and_2_out, and_3_out, and_4_out, AOUT, button_1_out, button_2_out, button_3_out,
       button_4_out, button_5_out, button_6_out, button_7_out, CI, CLK, clock_1_out, CMP, COL, CR, FCOL,
       GDRAW, GRESET, HLT, JNE, JOV, JPE, JZE, LFM, MO, N, not_1_out, or_1_out, or_3_out, or_4_out, or_5_out,
       ORI, P, R1_IN, R1_OUT, RADL, STM, SUB, V, XI, XO, YI, YO, Z;
  wire [2:0] MI_Counter_q;
  wire [3:0] nor_1_out;
  wire [7:0] au_1_sum, controlled_buffer_1_out, counter_1_q, Data_RAM_dout, OUT_Register_q, Program_ROM_data,
       Program_ROM_data_2, register_2_q, rgb_video_1_p4, rgb_video_1_p5, rgb_video_1_p6;

  or or_1 (or_1_out, button_1_out, GRESET);
  Button button_1 (.out(button_1_out));
  // RGB_Video #(.height(256), .width(256)) rgb_video_1: pin names not known; wires that end beside it: or_1_out, GDRAW, GDRAW, rgb_video_1_p4, rgb_video_1_p5, rgb_video_1_p6
  Clock clock_1 (.out(clock_1_out));
  Register #(.width(4)) register_1 (.D(nor_1_out), .en(CMP), .clk(CMP), .Q({V, N, Z, P}));  // open: clr
  nor nor_1 (nor_1_out[0], nor_1_out[1], nor_1_out[2]);
  or or_2 (CLK, clock_1_out, HLT);
  or or_3 (or_3_out, CMP, SUB);
  Register X_Register (.D(controlled_buffer_1_out), .en(XI), .clk(CLK), .Q(rgb_video_1_p4), .clr(button_2_out));
  Button button_2 (.out(button_2_out));
  Register Y_Register (.D(controlled_buffer_1_out), .en(YI), .clk(CLK), .Q(rgb_video_1_p5), .clr(button_3_out));
  Button button_3 (.out(button_3_out));
  Register R1_Register (.D(controlled_buffer_1_out), .en(R1_IN), .clk(CLK), .Q(rgb_video_1_p6), .clr(button_4_out));
  AU au_1 (
    .N2(rgb_video_1_p5), .N1(rgb_video_1_p4), .SUB(or_3_out), .C_OUT(nor_1_out[3]), .SUM(au_1_sum),
    .NEG(nor_1_out[2]), .ZERO(nor_1_out[1]));  // open: C_IN
  Button button_4 (.out(button_4_out));
  assign controlled_buffer_1_out = XO ? rgb_video_1_p4 : 8'bz;  // Controlled_Buffer controlled_buffer_1
  assign controlled_buffer_1_out = YO ? rgb_video_1_p5 : 8'bz;  // Controlled_Buffer controlled_buffer_2
  assign controlled_buffer_1_out = R1_OUT ? rgb_video_1_p6 : 8'bz;  // Controlled_Buffer controlled_buffer_3
  assign controlled_buffer_1_out = AOUT ? au_1_sum : 8'bz;  // Controlled_Buffer controlled_buffer_4
  assign controlled_buffer_1_out = MO ? Program_ROM_data : 8'bz;  // Controlled_Buffer controlled_buffer_5
  Counter #(.max('h7), .width(3)) MI_Counter (
    .Q(MI_Counter_q), .clk(CLK), .clr(CI));  // open: load, D, count, carry, up
  Register OUT_Register (.D(controlled_buffer_1_out), .en(ORI), .clk(CLK), .Q(OUT_Register_q), .clr(button_5_out));
  Button button_5 (.out(button_5_out));
  or or_4 (or_4_out, COL, FCOL, CI);
  assign controlled_buffer_1_out = CR ? counter_1_q : 8'bz;  // Controlled_Buffer controlled_buffer_6
  Register register_2 (.D(controlled_buffer_1_out), .en(RADL), .clk(CLK), .Q(register_2_q), .clr(button_7_out));
  Hex_Digit_Display hex_digit_display_1 (.value(OUT_Register_q[7:4]));  // open: dp
  PLA #(.in_width(11), .out_width(24), .\table ("00000000000 000000000000000000000000 # NOP\n00000000001 000000000000000000000010\n00000001000 000000000000100000000100 # LDX\n00000001001 000000000000000000000010\n00000010000 000000000000010000001000 # XOUT\n00000010001 000000000000000000000010\n00000011000 000000000000001000000100 # LDY\n00000011001 000000000000000000000010\n00000100000 000000000000000100001000 # YOUT\n00000100001 000000000000000000000010\n00000101000 000000000000000010000100 # LDR\n00000101001 000000000000000000000010\n00000110000 000000000000000001001000 # ROUT\n00000110001 000000000000000000000010\n00000111000 000000000000010010000000 # SWP\n00000111001 000000000000100100000000\n00000111010 000000000000001001000000\n00000111011 000000000000000000000010\n00001000000 000000000000000000101000 # AOUT\n00001000001 000000000000000000000010\n00001001000 000000000000000000111000 # SOUT\n00001001001 000000000000000000000010\n00001010000 000000000000000000000101 # JMP\n00001011000 000000000000000010100000 # ATX\n00001011001 000000000000100001000000\n00001011010 000000000000000000000010\n00001100000 000000000000000010100000 # ATY\n00001100001 000000000000001001000000\n00001100010 000000000000000000000010\n00001101000 000000000000000010110000 # STX\n00001101001 000000000000100001000000\n00001101010 000000000000000000000010\n00001110000 000000000000000010110000 # STY\n00001110001 000000000000001001000000\n00001110010 000000000000000000000010\n00001111000 000000000000010010000000 # XTR\n00001111001 000000000000000000000010\n00010000000 000000000000000110000000 # YTR\n00010000001 000000000000000000000010\n00010001000 000000000000100001000000 # RTX\n00010001001 000000000000000000000010\n00010010000 000000000000001001000000 # RTY\n00010010001 000000000000000000000010\n00010011000 000000000000000010100000 # ATR\n00010011001 000000000000000000000010\n00010100000 000000000000000010110000 # STR\n00010100001 000000000000000000000010\n00010101000 000000000010000000000100 # SAD\n00010101001 000000000000000000000010\n00010110000 000000000000000000000000 # XLM\n00010110001 000000000100100000000000\n00010110010 000000000000000000000010\n00010111000 000000001000010000000000 # XTM\n00010111001 000000000000000000000010\n00011000000 000000000000000000000000 # RLM\n00011000001 000000000100000010000000\n00011000010 000000000000000000000010\n00011001000 000000001000000001000000 # RTM\n00011001001 000000000000000000000010\n00011010000 000000000000000000000000 # YLM\n00011010001 000000000100001000000000\n00011010010 000000000000000000000010\n00011011000 000000001000000100000000 # YTM\n00011011001 000000000000000000000010\n00011100000 000000000010000001000000 # SADR\n00011100001 000000000000000000000010\n00011101000 000000000010010000000000 # SADX\n00011101001 000000000000000000000010\n00011110000 000000000010000100000000 # SADY\n00011110001 000000000000000000000010\n00011111000 000000010000000000000000 # CMP\n00011111001 000000000000000000000010\n00100000000 000000100000000000000100 # JNE\n00100000001 000000000000000000000010\n00100001000 000001000000000000000100 # JZE\n00100001001 000000000000000000000010\n00100010000 000010000000000000000100 # JOV\n00100010001 000000000000000000000010\n00100011000 000100000000000000000100 # JPE\n00100011001 000000000000000000000010\n00100100000 001000000000000000000000 # GDRAW\n00100100001 000000000000000000000010\n00100101000 010000000000000000000000 # GRESET\n00100101001 000000000000000000000010\n00100110000 100000000000000010000000 # PCR\n00100110001 000000000000000000000010\n00100111000 000000000000010000000001 # JTX\n10000000000 000000000001000000000000 # HLT")) MicroInstruction_PROM (
    .in({Program_ROM_data_2, MI_Counter_q}),
    .out({CR, GRESET, GDRAW, JPE, JOV, JZE, JNE, CMP, STM, LFM, RADL, HLT, XI, XO, YI, YO, R1_IN, R1_OUT, AOUT, SUB, ORI, MO, CI, COL}));
  Button button_6 (.out(button_6_out));
  Counter counter_1 (
    .clr(button_6_out), .load(or_5_out), .up(1'b1), .clk(or_4_out), .D(controlled_buffer_1_out),
    .Q(counter_1_q));  // open: count, carry
  or or_5 (or_5_out, FCOL, COL);
  Button button_7 (.out(button_7_out));
  Hex_Digit_Display hex_digit_display_2 (.value(OUT_Register_q[3:0]));  // open: dp
  ROM #(.dataWidth(16)) Program_ROM (.addr(counter_1_q), .data({Program_ROM_data_2, Program_ROM_data}));
  assign controlled_buffer_1_out = LFM ? Data_RAM_dout : 8'bz;  // Controlled_Buffer controlled_buffer_7
  RAM Data_RAM (
    .addr(register_2_q), .we(STM), .oe(not_1_out), .clk(CLK), .din(controlled_buffer_1_out),
    .dout(Data_RAM_dout));
  not not_1 (not_1_out, STM);
  and and_1 (and_1_out, JNE, N);
  and and_2 (and_2_out, JZE, Z);
  and and_3 (and_3_out, JOV, V);
  and and_4 (and_4_out, JPE, P);
  or or_6 (FCOL, and_1_out, and_2_out, and_3_out, and_4_out);

  // Notes on the sheet:
  //   Overflow, Negative, Zero, Positive
  //   Registers and AU
  //   BUS
  //   OpCode
  //   Data
  //   clear automatically
  //   on carry
  //   Instruction Control
  //   contents of Program_ROM (hex, n*v repeats v):
  //   a15 1500 1600 1502 1a00 1503 1800 2400 1501 1a00 1f00 210f 301 b00 a03 15ff 1600 304 b00 2700 8000
  //   2500 100 1500 1700 132 1501 1700 128 1502 1700 10a 1503 1700 2600 15ff 1900 a01 145 200 8000
  //   Program_ROM
  //   Comparison Jump Control
  //   Jump if Negative
  //   Jump if Zero
  //   Jump if Overflow
  //   Jump if Positive
endmodule
